# Fritzing sketch wiring_schematic (saved by Fritzing 0.9.9b)
breadboards: 1

parts:
  Mod1 = Raspberry Pi 4B
  R1 = Resistor [tolerance=±5% resistance=330 package="0402 [SMD]"]
  R2 = Resistor [tolerance=±5% resistance=10k package="0402 [SMD]"]
  LED1 = LED - 5mm [color="Red (633nm)" current=0.030 package="5 mm [THT]"]
  RHT1 = Humidity and Temperature Sensor RHT03

nets:
  5V: Mod1.5V, R1.Pin_0, R2.Pin_1, RHT1.Vcc
  N1: Mod1.GPIO2, R2.Pin_0, RHT1.Data-signal
  N2: Mod1.GND, RHT1.GND_2
  N3: Mod1.GPIO21, LED1.cathode
  N4: R1.Pin_1, LED1.anode
